// Logisim project accumulator.circ as structural Verilog: 8 circuits, main circuit main
module ALU (
  input  [15:0] B,
  input  [1:0] T,
  input  [15:0] A,
  output [15:0] S,
  output V,
  output Z,
  output C,
  output N
);

  wire and_1_out, and_2_out, xor_3_out;
  wire [15:0] adder_1_out, bit_extender_1_out, xor_1_out, xor_2_out;

  assign bit_extender_1_out = {{15{T[0]}}, T[0]};  // Bit_Extender bit_extender_1
  nor nor_1 (Z, S[0], S[1], S[2], S[3], S[4], S[5], S[6], S[7], S[9], S[10], S[11], S[12], S[13], S[14], N, S[8]);
  assign xor_1_out = bit_extender_1_out ^ B;  // XOR_Gate xor_1, 16 bits wide
  Adder #(.width(16)) adder_1 (.a(xor_1_out), .b(A), .out(adder_1_out), .cin(T[0]), .cout(C));
  assign xor_2_out = A ^ B;  // XOR_Gate xor_2, 16 bits wide
  MUX_4_1x16 mux_4_1x16_1 (
    .S1(T[1]), .S0(T[0]), .X0(adder_1_out), .X1(xor_2_out), .X2(B), .X3(adder_1_out), .Z({N, S[14:0]}));
  xor xor_3 (xor_3_out, B[15], T[0]);
  and and_1 (and_1_out, A[15], ~N, xor_3_out);  // AND_Gate
  and and_2 (and_2_out, ~xor_3_out, ~A[15], N);  // AND_Gate
  or or_1 (V, and_1_out, and_2_out);

  assign S[15] = N;

  // Other names for the same wires on the sheet: T_t = T[0]

  // Notes on the sheet:
  //   Cout16: 640ps
  //   55ps
  //   30ps
  //   FLAGS
  //   30ps
  //   MUX: 45ps
  //   Sum16: 660ps
  //   30ps
  //   20ps
  //   20ps
  //   20ps
  //   Retardo A=>Z: 790ps
  //   fmáx= 1.26Gop/s
endmodule

module MUX4_1 (
  input  S1,
  input  S0,
  input  X0,
  input  X1,
  input  X2,
  input  X3,
  output Z
);

  wire _20_ps_out, and_1_out, and_2_out, and_3_out, not_1_out, not_2_out, not_3_out, not_4_out;

  not not_1 (not_1_out, S1);
  not not_2 (not_2_out, S0);
  not not_3 (not_3_out, S1);
  not not_4 (not_4_out, S0);
  and _20_ps (_20_ps_out, not_1_out, not_2_out, X0);
  and and_1 (and_1_out, not_3_out, S0, X1);
  and and_2 (and_2_out, S1, not_4_out, X2);
  and and_3 (and_3_out, S1, S0, X3);
  or or_1 (Z, _20_ps_out, and_1_out, and_2_out, and_3_out);

  // Notes on the sheet:
  //   5ps
  //   5ps
  //   5ps
  //   5ps
  //   Retardo: 45 ps
  //   20ps
  //   20ps
  //   20ps
  //   20ps
endmodule

module MUX_4_1x4 (
  input  S1,
  input  S0,
  input  [3:0] X0,
  input  [3:0] X1,
  input  [3:0] X2,
  input  [3:0] X3,
  output [3:0] Z
);

  MUX4_1 mux4_1_1 (.S1(S1), .S0(S0), .X0(X0[0]), .X1(X1[0]), .X2(X2[0]), .X3(X3[0]), .Z(Z[0]));
  MUX4_1 mux4_1_2 (.S1(S1), .S0(S0), .X0(X0[1]), .X1(X1[1]), .X2(X2[1]), .X3(X3[1]), .Z(Z[1]));
  MUX4_1 mux4_1_3 (.S1(S1), .S0(S0), .X0(X0[2]), .X1(X1[2]), .X2(X2[2]), .X3(X3[2]), .Z(Z[2]));
  MUX4_1 mux4_1_4 (.S1(S1), .S0(S0), .X0(X0[3]), .X1(X1[3]), .X2(X2[3]), .X3(X3[3]), .Z(Z[3]));

  // Notes on the sheet:
  //   Retardo: 45 ps
endmodule

module MUX_4_1x16 (
  input  S1,
  input  S0,
  input  [15:0] X0,
  input  [15:0] X1,
  input  [15:0] X2,
  input  [15:0] X3,
  output [15:0] Z
);

  MUX_4_1x4 mux_4_1x4_1 (.S1(S1), .S0(S0), .X0(X0[3:0]), .X1(X1[3:0]), .X2(X2[3:0]), .X3(X3[3:0]), .Z(Z[3:0]));
  MUX_4_1x4 mux_4_1x4_2 (.S1(S1), .S0(S0), .X0(X0[7:4]), .X1(X1[7:4]), .X2(X2[7:4]), .X3(X3[7:4]), .Z(Z[7:4]));
  MUX_4_1x4 mux_4_1x4_3 (.S1(S1), .S0(S0), .X0(X0[11:8]), .X1(X1[11:8]), .X2(X2[11:8]), .X3(X3[11:8]), .Z(Z[11:8]));
  MUX_4_1x4 mux_4_1x4_4 (
    .S1(S1), .S0(S0), .X0(X0[15:12]), .X1(X1[15:12]), .X2(X2[15:12]), .X3(X3[15:12]), .Z(Z[15:12]));

  // Notes on the sheet:
  //   Retardo: 45ps
endmodule

module AddGen (
  input  reset_star,
  input  clk,
  input  ag_en,
  output q2,
  output q1,
  output q0,
  output \end 
);

  wire and_1_out, and_2_out, and_3_out, and_4_out, not_1_out, not_2_out, not_3_out, not_4_out, or_1_out,
       or_2_out, or_3_out, or_4_out, or_5_out;

  not not_1 (not_1_out, ag_en);
  not not_2 (not_2_out, q2);
  not not_3 (not_3_out, q1);
  not not_4 (not_4_out, q0);
  or or_1 (or_1_out, ag_en, q2);
  or or_2 (or_2_out, q2, q1);
  or or_3 (or_3_out, q2, q0);
  or or_4 (or_4_out, not_1_out, not_2_out, not_3_out, not_4_out);
  and and_1 (and_1_out, ag_en, q0, not_3_out);
  and and_2 (and_2_out, not_1_out, q1);
  and and_3 (and_3_out, not_4_out, q1);
  and and_4 (and_4_out, or_1_out, or_2_out, or_3_out, or_4_out);
  or or_5 (or_5_out, and_1_out, and_2_out, and_3_out);
  D_Flip_Flop d_ff_1 (.clk(clk), .D(and_4_out), .Q(q2), .reset(reset_star));  // open: Qn, preset, en
  D_Flip_Flop d_ff_2 (.clk(clk), .D(or_5_out), .Q(q1), .reset(reset_star));  // open: Qn, preset, en
  T_Flip_Flop t_ff_1 (.clk(clk), .T(ag_en), .Q(q0), .reset(reset_star));  // open: Qn, preset, en
  and _20ps (\end , q2, q1, q0);
endmodule

module main (
  input  [1:0] flag,
  input  reset_star,
  output [15:0] ACC
);

  wire acc_en, ag_en, C, clk, \end , mdr_en, N, stop, V, Z;
  wire [2:0] addgen_1_q0;
  wire [15:0] MDR_q, rom_1_data, S;

  Clock u_clk (.out(clk));
  FD fd_1 (.flag(flag), .V(V), .Z(Z), .C(C), .N(N), .stop(stop));
  U_C u_c_1 (
    .\end (\end ), .stop(stop), .clk(clk), .reset_star(reset_star), .ag_en(ag_en), .mdr_en(mdr_en),
    .acc_en(acc_en));
  AddGen addgen_1 (
    .reset_star(reset_star), .clk(clk), .ag_en(ag_en), .q2(addgen_1_q0[2]), .q1(addgen_1_q0[1]),
    .q0(addgen_1_q0[0]), .\end (\end ));
  ROM #(.addrWidth(3), .dataWidth(16)) rom_1 (.addr(addgen_1_q0), .data(rom_1_data));  // open: sel
  Register #(.width(16)) MDR (.D(rom_1_data), .en(mdr_en), .Q(MDR_q), .clk(clk), .clr(reset_star));
  ALU alu_1 (.B(MDR_q), .T(flag), .A(ACC), .S(S), .V(V), .Z(Z), .C(C), .N(N));
  Register #(.width(16)) u_ACC (.D(S), .en(acc_en), .Q(ACC), .clk(clk), .clr(reset_star));
  // Probe on ACC

  // Notes on the sheet:
  //   45
  //   75
  //   80
  //   50
  //   130
  //   110
  //   70
  //   30
  //   contents of rom_1 (hex, n*v repeats v):
  //   fff0 2 3 4 5 6 7 8
  //   30
  //   50
  //   50
  //   790
  //   fmáx=1.714GHz
  //   Tmin(clk)=1075ps
endmodule

module U_C (
  input  \end ,
  input  stop,
  input  clk,
  input  reset_star,
  output ag_en,
  output mdr_en,
  output acc_en
);

  wire [1:0] register_1_q, rom_1_data;

  ROM #(.addrWidth(4), .dataWidth(2)) rom_1 (.addr({register_1_q, stop, \end }), .data(rom_1_data));  // open: sel
  Register #(.width(2)) register_1 (.D(rom_1_data), .Q(register_1_q), .clk(clk), .clr(reset_star));  // open: en
  ROM #(.addrWidth(2), .dataWidth(3)) rom_2 (.addr(register_1_q), .data({acc_en, mdr_en, ag_en}));  // open: sel

  // Notes on the sheet:
  //   contents of rom_1 (hex, n*v repeats v):
  //   2 0 1 3 2 0 3 3 2 3 1 3 2 0 3 3
  //   contents of rom_2 (hex, n*v repeats v):
  //   2 5
endmodule

module FD (
  input  [1:0] flag,
  input  V,
  input  Z,
  input  C,
  input  N,
  output stop
);

  MUX4_1 mux4_1_1 (.S1(flag[0]), .S0(flag[1]), .X0(V), .X1(Z), .X2(C), .X3(N), .Z(stop));

  // Notes on the sheet:
  //   MUX 4:1 = 45ps
endmodule
