// Logisim project alu.circ as structural Verilog: 4 circuits, main circuit MUX4:1
module main (
  input  [15:0] B,
  input  [1:0] T,
  input  [15:0] A,
  output [15:0] S,
  output V,
  output Z,
  output C,
  output N
);

  wire and_1_out, and_2_out, xor_3_out;
  wire [15:0] adder_1_out, bit_extender_1_out, xor_1_out, xor_2_out;

  assign bit_extender_1_out = {{15{T[0]}}, T[0]};  // Bit_Extender bit_extender_1
  nor nor_1 (Z, S[0], S[1], S[2], S[3], S[4], S[5], S[6], S[7], S[9], S[10], S[11], S[12], S[13], S[14], N, S[8]);
  assign xor_1_out = bit_extender_1_out ^ B;  // XOR_Gate xor_1, 16 bits wide
  Adder #(.width(16)) adder_1 (.a(xor_1_out), .b(A), .out(adder_1_out), .cin(T[0]), .cout(C));
  assign xor_2_out = A ^ B;  // XOR_Gate xor_2, 16 bits wide
  MUX_4_1x16 mux_4_1x16_1 (
    .S1(T[1]), .S0(T[0]), .X0(adder_1_out), .X1(xor_2_out), .X2(B), .X3(adder_1_out), .Z({N, S[14:0]}));
  xor xor_3 (xor_3_out, B[15], T[0]);
  and and_1 (and_1_out, A[15], ~N, xor_3_out);  // AND_Gate
  and and_2 (and_2_out, ~xor_3_out, ~A[15], N);  // AND_Gate
  or or_1 (V, and_1_out, and_2_out);

  assign S[15] = N;

  // Other names for the same wires on the sheet: T_t = T[0]

  // Notes on the sheet:
  //   Cout16: 640ps
  //   55ps
  //   30ps
  //   FLAGS
  //   30ps
  //   Sum16: 660ps
  //   MUX: 45ps
  //   30ps
  //   20ps
  //   20ps
  //   20ps
  //   Retardo A=>Z: 790ps
  //   fmáx= 1.26Gop/s
endmodule

module MUX4_1 (
  input  S1,
  input  S0,
  input  X0,
  input  X1,
  input  X2,
  input  X3,
  output Z
);

  wire _20_ps_out, and_1_out, and_2_out, and_3_out, not_1_out, not_2_out, not_3_out, not_4_out;

  not not_1 (not_1_out, S1);
  not not_2 (not_2_out, S0);
  not not_3 (not_3_out, S1);
  not not_4 (not_4_out, S0);
  and _20_ps (_20_ps_out, not_1_out, not_2_out, X0);
  and and_1 (and_1_out, not_3_out, S0, X1);
  and and_2 (and_2_out, S1, not_4_out, X2);
  and and_3 (and_3_out, S1, S0, X3);
  or or_1 (Z, _20_ps_out, and_1_out, and_2_out, and_3_out);

  // Notes on the sheet:
  //   5ps
  //   5ps
  //   5ps
  //   5ps
  //   Retardo: 45 ps
  //   20ps
  //   20ps
  //   20ps
  //   20ps
endmodule

module MUX_4_1x4 (
  input  S1,
  input  S0,
  input  [3:0] X0,
  input  [3:0] X1,
  input  [3:0] X2,
  input  [3:0] X3,
  output [3:0] Z
);

  MUX4_1 mux4_1_1 (.S1(S1), .S0(S0), .X0(X0[0]), .X1(X1[0]), .X2(X2[0]), .X3(X3[0]), .Z(Z[0]));
  MUX4_1 mux4_1_2 (.S1(S1), .S0(S0), .X0(X0[1]), .X1(X1[1]), .X2(X2[1]), .X3(X3[1]), .Z(Z[1]));
  MUX4_1 mux4_1_3 (.S1(S1), .S0(S0), .X0(X0[2]), .X1(X1[2]), .X2(X2[2]), .X3(X3[2]), .Z(Z[2]));
  MUX4_1 mux4_1_4 (.S1(S1), .S0(S0), .X0(X0[3]), .X1(X1[3]), .X2(X2[3]), .X3(X3[3]), .Z(Z[3]));

  // Notes on the sheet:
  //   Retardo: 45 ps
endmodule

module MUX_4_1x16 (
  input  S1,
  input  S0,
  input  [15:0] X0,
  input  [15:0] X1,
  input  [15:0] X2,
  input  [15:0] X3,
  output [15:0] Z
);

  MUX_4_1x4 mux_4_1x4_1 (.S1(S1), .S0(S0), .X0(X0[3:0]), .X1(X1[3:0]), .X2(X2[3:0]), .X3(X3[3:0]), .Z(Z[3:0]));
  MUX_4_1x4 mux_4_1x4_2 (.S1(S1), .S0(S0), .X0(X0[7:4]), .X1(X1[7:4]), .X2(X2[7:4]), .X3(X3[7:4]), .Z(Z[7:4]));
  MUX_4_1x4 mux_4_1x4_3 (.S1(S1), .S0(S0), .X0(X0[11:8]), .X1(X1[11:8]), .X2(X2[11:8]), .X3(X3[11:8]), .Z(Z[11:8]));
  MUX_4_1x4 mux_4_1x4_4 (
    .S1(S1), .S0(S0), .X0(X0[15:12]), .X1(X1[15:12]), .X2(X2[15:12]), .X3(X3[15:12]), .Z(Z[15:12]));

  // Notes on the sheet:
  //   Retardo: 45ps
endmodule
