// Logisim project integerDisplay.circ as structural Verilog: 3 circuits, main circuit tabla
module main (
  input  x0,
  input  x1,
  input  x2,
  input  x3,
  input  y3,
  input  y2,
  input  y1,
  input  y0
);

  wire a, ax, ay, b, bx, by, c, cx, cy, d, dx, dy, e, ex, ey, f, fx, fy, g, gx, gy, rca4_1_s0, rca4_1_s1,
       rca4_1_s2, rca4_1_s3, s, sx, sy;

  tabla tabla_1 (.x3(x3), .x2(x2), .x1(x1), .x0(x0), .s(sx), .a(ax), .b(bx), .c(cx), .d(dx), .e(ex), .f(fx), .g(gx));
  RCA4 rca4_1 (
    .x2(x2), .x0(x0), .x3(x3), .x1(x1), .y2(y2), .y0(y0), .y3(y3), .y1(y1), .S2(rca4_1_s2), .S0(rca4_1_s0),
    .S3(rca4_1_s3), .S1(rca4_1_s1));
  tabla tabla_2 (.x3(y3), .x2(y2), .x1(y1), .x0(y0), .s(sy), .a(ay), .b(by), .c(cy), .d(dy), .e(ey), .f(fy), .g(gy));
  tabla tabla_3 (
    .x3(rca4_1_s3), .x2(rca4_1_s2), .x1(rca4_1_s1), .x0(rca4_1_s0), .s(s), .a(a), .b(b), .c(c), .d(d), .e(e),
    .f(f), .g(g));
  _7_Segment_Display u_7_segment_display_1 (.g(sx));  // open: f, a, b, e, d, c, dp
  _7_Segment_Display u_7_segment_display_2 (.g(sy));  // open: f, a, b, e, d, c, dp
  _7_Segment_Display u_7_segment_display_3 (.g(gx), .f(fx), .a(ax), .b(bx), .e(ex), .d(dx), .c(cx));  // open: dp
  _7_Segment_Display u_7_segment_display_4 (.g(gy), .f(fy), .a(ay), .b(by), .e(ey), .d(dy), .c(cy));  // open: dp
  _7_Segment_Display u_7_segment_display_5 (.g(s));  // open: f, a, b, e, d, c, dp
  _7_Segment_Display u_7_segment_display_6 (.g(g), .f(f), .a(a), .b(b), .e(e), .d(d), .c(c));  // open: dp

  // Notes on the sheet:
  //   x3: pull=up
  //   x2: pull=up
  //   y0: pull=up
  //   y2: pull=up
  //   y1: pull=up
  //   y3: pull=up
  //   x1: pull=up
  //   x0: pull=up
endmodule

module tabla (
  input  x3,
  input  x2,
  input  x1,
  input  x0,
  output s,
  output a,
  output b,
  output c,
  output d,
  output e,
  output f,
  output g
);

  wire and_1_out, and_2_out, and_3_out, and_4_out, and_5_out, and_6_out, and_7_out, and_8_out, and_9_out,
       and_10_out, and_11_out, and_12_out, and_13_out, and_14_out, and_15_out, not_1_out, not_2_out,
       not_3_out, not_4_out, not_5_out, not_6_out, not_7_out, not_8_out, not_9_out, not_10_out, not_11_out,
       not_12_out, not_13_out, not_14_out, not_15_out, not_16_out, not_17_out, not_18_out, not_19_out,
       not_20_out, not_21_out, not_22_out, not_23_out, not_24_out, not_25_out, not_26_out, not_27_out,
       not_28_out, not_29_out, not_30_out, not_31_out, not_32_out, not_33_out, not_34_out, not_35_out,
       not_36_out, not_37_out, not_38_out, or_1_out, or_2_out, or_3_out, or_4_out, or_5_out, or_6_out,
       or_7_out, or_8_out, or_9_out, or_14_out, or_15_out;

  and and_1 (and_1_out, x3, not_1_out);
  not not_1 (not_1_out, x2);
  and and_2 (and_2_out, x3, not_2_out);
  not not_2 (not_2_out, x0);
  and and_3 (and_3_out, x3, x1);
  not not_3 (not_3_out, x2);
  and and_4 (and_4_out, not_3_out, not_4_out);
  not not_4 (not_4_out, x0);
  not not_5 (not_5_out, x3);
  and and_5 (and_5_out, not_5_out, x1);
  and and_6 (and_6_out, x1, not_6_out);
  not not_6 (not_6_out, x0);
  not not_7 (not_7_out, x1);
  and and_7 (and_7_out, x2, not_7_out, x0);
  and and_8 (and_8_out, x3, not_8_out);
  not not_8 (not_8_out, x2);
  not not_9 (not_9_out, x3);
  and and_9 (and_9_out, not_9_out, not_10_out);
  not not_10 (not_10_out, x2);
  not not_11 (not_11_out, x2);
  and and_10 (and_10_out, not_11_out, not_12_out);
  not not_12 (not_12_out, x1);
  not not_13 (not_13_out, x1);
  and and_11 (and_11_out, not_13_out, not_14_out);
  not not_14 (not_14_out, x0);
  not not_15 (not_15_out, x3);
  and and_12 (and_12_out, not_15_out, x1, x0);
  and and_13 (and_13_out, x3, x2);
  not not_16 (not_16_out, x1);
  not not_17 (not_17_out, x3);
  and and_14 (and_14_out, not_17_out, x2);
  and and_15 (and_15_out, x3, not_18_out);
  not not_18 (not_18_out, x2);
  or or_1 (or_1_out, x2, x1, not_19_out);
  not not_19 (not_19_out, x0);
  not not_20 (not_20_out, x2);
  or or_2 (or_2_out, not_20_out, x1, x0);
  not not_21 (not_21_out, x2);
  or or_3 (or_3_out, not_21_out, not_22_out, not_23_out);
  not not_22 (not_22_out, x1);
  not not_23 (not_23_out, x0);
  not not_24 (not_24_out, x0);
  not not_25 (not_25_out, x2);
  or or_4 (or_4_out, not_25_out, x1);
  or or_5 (or_5_out, x2, x1, not_26_out);
  not not_26 (not_26_out, x0);
  or or_6 (or_6_out, x3, x2, not_27_out);
  not not_27 (not_27_out, x1);
  or or_7 (or_7_out, x3, not_28_out, not_29_out);
  not not_28 (not_28_out, x1);
  not not_29 (not_29_out, x0);
  not not_30 (not_30_out, x3);
  or or_8 (or_8_out, not_30_out, x1, not_31_out);
  not not_31 (not_31_out, x0);
  not not_32 (not_32_out, x3);
  not not_33 (not_33_out, x2);
  or or_9 (or_9_out, not_32_out, not_33_out, not_34_out);
  not not_34 (not_34_out, x1);
  not not_35 (not_35_out, x3);
  not not_36 (not_36_out, x2);
  not not_37 (not_37_out, x1);
  not not_38 (not_38_out, x0);
  or or_10 (s, and_1_out, and_2_out, and_3_out);
  or or_11 (a, and_4_out, and_5_out, and_6_out, and_7_out, and_8_out);
  or or_12 (b, and_9_out, and_10_out, and_11_out, and_12_out, and_13_out);
  or or_13 (c, not_16_out, x0, and_14_out, and_15_out);
  and and_16 (d, or_1_out, or_2_out, or_3_out);
  and and_17 (e, not_24_out, or_4_out);
  and and_18 (f, or_5_out, or_6_out, or_7_out, or_8_out, or_9_out);
  or or_14 (or_14_out, x3, x2, x1);
  and and_19 (g, or_14_out, or_15_out);
  or or_15 (or_15_out, not_35_out, not_36_out, not_37_out, not_38_out);
endmodule

module RCA4 (
  input  x2,
  input  x0,
  input  x3,
  input  x1,
  input  y2,
  input  y0,
  input  y3,
  input  y1,
  output S2,
  output S0,
  output S3,
  output S1
);

  wire and_1_out, and_2_out, and_3_out, and_4_out, and_5_out, and_6_out, and_7_out, and_8_out, or_1_out,
       or_2_out, or_3_out, xor_1_out, xor_3_out, xor_5_out, xor_7_out, Z;

  xor xor_1 (xor_1_out, x0, y0);
  and and_1 (and_1_out, y0, x0);
  and and_2 (and_2_out, 1'b0, xor_1_out);
  xor xor_2 (S0, xor_1_out, 1'b0);
  or or_1 (or_1_out, and_2_out, and_1_out);
  xor xor_3 (xor_3_out, x1, y1);
  and and_3 (and_3_out, y1, x1);
  xor xor_4 (S1, xor_3_out, or_1_out);
  and and_4 (and_4_out, or_1_out, xor_3_out);
  or or_2 (or_2_out, and_4_out, and_3_out);
  xor xor_5 (xor_5_out, x2, y2);
  and and_5 (and_5_out, y2, x2);
  xor xor_6 (S2, xor_5_out, or_2_out);
  and and_6 (and_6_out, or_2_out, xor_5_out);
  or or_3 (or_3_out, and_6_out, and_5_out);
  xor xor_7 (xor_7_out, x3, y3);
  and and_7 (and_7_out, y3, x3);
  and and_8 (and_8_out, or_3_out, xor_7_out);
  xor xor_8 (S3, xor_7_out, or_3_out);
  or or_4 (Z, and_8_out, and_7_out);
endmodule
