// Logisim project logicGates.circ as structural Verilog: 1 circuit, main circuit main
module main (
  input  a,
  input  b,
  input  c,
  input  d,
  output z,
  output z2,
  output z3
);

  wire and_1_out, and_2_out, and_3_out, and_4_out, and_5_out, and_6_out, and_7_out, and_8_out, and_9_out,
       and_11_out, and_12_out, and_13_out, and_14_out, and_15_out, nor_1_out, not_1_out, not_2_out,
       not_3_out, not_4_out, not_6_out, not_7_out, not_8_out, not_9_out, or_1_out, or_2_out;

  not not_1 (not_1_out, a);
  not not_2 (not_2_out, b);
  not not_3 (not_3_out, c);
  not not_4 (not_4_out, d);
  and and_1 (and_1_out, a, b);
  and and_2 (and_2_out, c, d);
  and and_3 (and_3_out, d, a);
  and and_4 (and_4_out, b, c);
  and and_5 (and_5_out, not_1_out, b, c, d);
  and and_6 (and_6_out, a, not_2_out, c, d);
  and and_7 (and_7_out, a, b, not_3_out, d);
  and and_8 (and_8_out, a, b, c, not_4_out);
  and and_9 (and_9_out, a, b, c, d);
  or or_1 (or_1_out, and_1_out, and_2_out);
  or or_2 (or_2_out, and_3_out, and_4_out);
  and and_10 (z, or_1_out, or_2_out);
  nor nor_1 (nor_1_out, and_5_out, and_6_out, and_7_out, and_8_out, and_9_out);
  not not_5 (z3, nor_1_out);
  not not_6 (not_6_out, a);
  not not_7 (not_7_out, b);
  not not_8 (not_8_out, c);
  not not_9 (not_9_out, d);
  and and_11 (and_11_out, not_6_out, b, c, d);
  and and_12 (and_12_out, a, b, c, not_9_out);
  and and_13 (and_13_out, a, b, c, d);
  and and_14 (and_14_out, a, not_7_out, c, d);
  and and_15 (and_15_out, a, b, not_8_out, d);
  or or_3 (z2, and_11_out, and_14_out, and_15_out, and_12_out, and_13_out);

  // Notes on the sheet:
  //   z3: pull=down
  //   c: pull=down
  //   d: pull=down
  //   z: pull=down
  //   z2: pull=down
  //   b: pull=down
  //   a: pull=down
endmodule
