// Logisim project turing_machine_tty-4.circ as structural Verilog: 5 circuits, main circuit main
module MUX_4_1 (
  input  X0,
  input  X1,
  input  X2,
  input  X3,
  input  S0,
  input  S1,
  output Z
);

  wire _20_2_out, _20_3_out, _20_4_out, _20_out, not_1_out, not_2_out;

  not not_1 (not_1_out, S0);
  not not_2 (not_2_out, S1);
  and _20 (_20_out, X0, not_2_out, not_1_out);
  and _20_2 (_20_2_out, X1, S0, not_2_out);
  and _20_3 (_20_3_out, X2, S1, not_1_out);
  and _20_4 (_20_4_out, X3, S0, S1);
  or _20_5 (Z, _20_out, _20_2_out, _20_3_out, _20_4_out);

  // Notes on the sheet:
  //   5
  //   5
  //   dXo --> z = 45 ps
  //   dX1 --> z = 45 ps
  //   dX2 --> z = 45 ps
  //   dX3 --> z = 45 ps
endmodule

module MUX_4_1x4 (
  input  S0,
  input  S1,
  input  [3:0] X0,
  input  [3:0] X1,
  input  [3:0] X2,
  input  [3:0] X3,
  output [3:0] Z
);

  MUX_4_1 mux_4_1_1 (.X0(X0[0]), .X1(X1[0]), .X2(X2[0]), .X3(X3[0]), .S0(S0), .S1(S1), .Z(Z[0]));
  MUX_4_1 mux_4_1_2 (.X0(X0[1]), .X1(X1[1]), .X2(X2[1]), .X3(X3[1]), .S0(S0), .S1(S1), .Z(Z[1]));
  MUX_4_1 mux_4_1_3 (.X0(X0[2]), .X1(X1[2]), .X2(X2[2]), .X3(X3[2]), .S0(S0), .S1(S1), .Z(Z[2]));
  MUX_4_1 mux_4_1_4 (.X0(X0[3]), .X1(X1[3]), .X2(X2[3]), .X3(X3[3]), .S0(S0), .S1(S1), .Z(Z[3]));

  // Notes on the sheet:
  //   dx0->z = 180 ps
  //   dx3->z = 180 ps
  //   dx1->z = 180 ps
  //   dx2->z = 180 ps
  //   45
  //   45
  //   45
  //   45
endmodule

module MUX_4_1x16 (
  input  [15:0] X0,
  input  [15:0] X1,
  input  [15:0] X2,
  input  [15:0] X3,
  input  S0,
  input  S1,
  output [15:0] Z
);

  MUX_4_1x4 mux_4_1x4_1 (.S0(S0), .S1(S1), .X0(X0[3:0]), .X1(X1[3:0]), .X2(X2[3:0]), .X3(X3[3:0]), .Z(Z[3:0]));
  MUX_4_1x4 mux_4_1x4_2 (.S0(S0), .S1(S1), .X0(X0[7:4]), .X1(X1[7:4]), .X2(X2[7:4]), .X3(X3[7:4]), .Z(Z[7:4]));
  MUX_4_1x4 mux_4_1x4_3 (.S0(S0), .S1(S1), .X0(X0[11:8]), .X1(X1[11:8]), .X2(X2[11:8]), .X3(X3[11:8]), .Z(Z[11:8]));
  MUX_4_1x4 mux_4_1x4_4 (
    .S0(S0), .S1(S1), .X0(X0[15:12]), .X1(X1[15:12]), .X2(X2[15:12]), .X3(X3[15:12]), .Z(Z[15:12]));

  // Notes on the sheet:
  //   dX0 --> z = 720 ps
  //   dX1 --> z = 720 ps
  //   dX2 --> z = 720 ps
  //   dX23--> z = 720 ps
  //   180
  //   180
  //   180
  //   180
endmodule

module ALU (
  input  [1:0] T,
  input  [15:0] A,
  input  [15:0] B,
  output [15:0] S,
  output C,
  output V,
  output N,
  output Z
);

  wire _20_2_out, _20_out, _30_out, not_1_out, not_2_out, not_3_out;
  wire [15:0] _30_2_out, _30_3_out, adder_1_out, bit_extender_1_out;

  xor _30 (_30_out, T[0], B[15]);
  assign bit_extender_1_out = {{15{T[1]}}, T[1]};  // Bit_Extender bit_extender_1
  not not_1 (not_1_out, N);
  not not_2 (not_2_out, _30_out);
  not not_3 (not_3_out, A[15]);
  assign _30_2_out = bit_extender_1_out ^ B;  // XOR_Gate _30_2, 16 bits wide
  and _20 (_20_out, not_1_out, _30_out, A[15]);
  and _20_2 (_20_2_out, N, not_2_out, not_3_out);
  Adder #(.width(16)) adder_1 (.a(A), .b(_30_2_out), .out(adder_1_out), .cin(T[1]), .cout(C));
  assign _30_3_out = A ^ B;  // XOR_Gate _30_3, 16 bits wide
  or _20_3 (V, _20_out, _20_2_out);
  MUX_4_1x16 mux_4_1x16_1 (
    .X0(adder_1_out), .X1(_30_3_out), .X2(B), .X3(adder_1_out), .S0(T[0]), .S1(T[1]), .Z({N, S[14:0]}));
  nor _55 (Z, N, S[14], S[13], S[12], S[11], S[10], S[9], S[8], S[7], S[6], S[5], S[4], S[3], S[2], S[1], S[0]);

  assign S[15] = N;

  // Other names for the same wires on the sheet: Suma[15:0] = {N, S[14:0]}

  // Notes on the sheet:
  //   5
  //   5
  //   5
  //   0
  //   0
  //   70
  //   30
  //   90
  //   55
  //   25
  //   75
  //   40, 40, 0, 70, 0, 0
  //   720
  //   790
endmodule

module main (
);

  wire a_t, alu_1_z, and_1_out, and_2_out, and_3_out, b, clk, d_ff_1_q, FZ, fz_t, ir, nL_E, not_1_out, pc_t,
       reset;
  wire [1:0] alu, mux;
  wire [3:0] CO, estado, rom_1_data;
  wire [4:0] F;
  wire [6:0] A, adder_1_out, D, D6_0, PC;
  wire [15:0] A_q, B_q, ram_1_data;
  wire [15:7] alu_1_s;

  Register #(.width(4)) u_estado (.D(rom_1_data), .Q(estado), .clk(clk), .clr(reset));  // open: en
  Register #(.width(7)) u_PC (.D(adder_1_out), .en(pc_t), .Q(PC), .clk(clk), .clr(reset));
  Register #(.width(16)) u_IR (.D(ram_1_data), .en(ir), .Q({CO, F, D}), .clk(clk));  // open: clr
  Multiplexer #(.select(2), .width(7), .enable("false")) multiplexer_1 (
    .in0(PC), .in2({CO[1:0], F}), .in3(D), .out(A), .sel(mux));  // open: in1
  ROM #(.addrWidth(9), .dataWidth(4)) rom_1 (.addr({estado, CO, FZ}), .data(rom_1_data));  // open: sel
  ROM #(.addrWidth(4), .dataWidth(10)) rom_2 (
    .addr(estado), .data({mux, alu, nL_E, pc_t, ir, a_t, b, fz_t}));  // open: sel
  Adder #(.width(7)) adder_1 (.a(7'b0000001), .b(A), .out(adder_1_out));  // open: cin, cout
  Register #(.width(16)) u_A (.D(ram_1_data), .en(a_t), .Q(A_q), .clk(clk));  // open: clr
  Register #(.width(1)) u_FZ (.D(alu_1_z), .en(fz_t), .Q(FZ), .clk(clk));  // open: clr
  ALU alu_1 (.T(alu), .A(A_q), .B(B_q), .Z(alu_1_z), .S({alu_1_s, D6_0}));  // open: C, V, N
  // Probe on PC
  // Probe on CO
  Register #(.width(16)) u_B (.D(ram_1_data), .en(b), .Q(B_q), .clk(clk));  // open: clr
  Button button_1 (.out(reset));
  Clock clock_1 (.out(clk));
  // Probe on D
  // Probe on {CO[1:0], F}
  and and_1 (and_1_out, A[0], A[1], A[2], A[3], A[4], A[5], A[6], nL_E);
  and and_2 (and_2_out, and_1_out, and_3_out);
  and and_3 (and_3_out, ~D6_0[0], ~D6_0[1], ~D6_0[2], ~D6_0[3], ~D6_0[4], ~D6_0[5], ~D6_0[6]);  // AND_Gate
  RAM #(.addrWidth(7), .dataWidth(16), .bus("separate")) ram_1 (
    .addr(A), .din({alu_1_s, D6_0}), .data(ram_1_data), .str(nL_E), .sel(1'b1), .clk(clk), .ld(not_1_out));  // open: clr
  not not_1 (not_1_out, nL_E);
  // Probe on estado
  TTY tty_1 (.data(D6_0), .clk(clk), .we(and_1_out), .clr(d_ff_1_q));
  D_Flip_Flop d_ff_1 (.clk(clk), .D(and_2_out), .Q(d_ff_1_q), .en(1'b1));  // open: Qn, preset, reset

  // Other names for the same wires on the sheet: F[6:5] = CO[1:0]

  // Notes on the sheet:
  //   Unidad de Control (cableada 12 estados)
  //   Unidad de Proceso (ruta de datos)
  //   contents of rom_1 (hex, n*v repeats v):
  //   32*1 8*2 8*3 8*4 5 5 b b 5 5 b b 32*6 32*8 32*a 0 b 0 b b 0 b 0 0 b 0 b b 0 b 0 0 b 0 b b 0 b 0 0 b
  //   0 b b 0 b 0 32*7 32*0 32*9 64*0 32*1
  //   contents of rom_2 (hex, n*v repeats v):
  //   18 0 202 202 202 0 304 321 304 41 3a1 318
  //   0 ADD
  //   1 CMP
  //   2 MOV
  //   12 BEQ
  //   14 BNEQ
  //   15 B
  //   Control de simulación
endmodule
